# Fritzing sketch Master_slave_setup (saved by Fritzing 0.9.10b)
breadboards: 1

parts:
  Mod1 = Amica NodeMCU DEVKIT 1.0
  Part1 = Arduino Uno (Rev3)
  Keypad4x2 = Keypad Membran 4x4
  YwRobot_Power_Supply1 = YwRobot Breadboard Power Supply [part_number=545043]
  R1 = Photocell (LDR) [package=THT]
  R2 = Resistor [tolerance=±5% power=0.25 resistance=220 package=THT]
  M1 = Dagu DGServo 9g (Top view) [part_number=RS001B]
  Part2 = RFID-RC522-v2
  LED1 = smd LED [color="Green (565nm)" package="0603 [SMD]"]
  LED2 = smd LED [color="Red (633nm)" package="0603 [SMD]"]
  R3 = Resistor [tolerance=±5% power=0.25 resistance=220 package=THT]
  R4 = Resistor [tolerance=±5% power=0.25 resistance=220 package=THT]

nets:
  VCC: Mod1.pin1, Mod1.pin_10, Mod1.pin_26, M1.vcc, Part2.3.3V
  GND: Mod1.pin2, Mod1.pin_9, Mod1.pin_25, Mod1.pin_29, Part1.GND, YwRobot_Power_Supply1.GND, R2.Pin_0, M1.gnd, Part2.GND, R3.Pin_0, R4.Pin_0
  N1: Mod1.pin3, LED2.anode
  N2: Mod1.pin5, M1.pulse
  N3: Mod1.pin6, Part2.MOSI
  N4: Mod1.pin7, Part2.MISO
  N5: Mod1.pin8, Part2.SCK
  N6: Mod1.pin_11, Part2.SDA
  N7: Mod1.pin_12, Part2.RST
  N8: Mod1.pin_13, Part1.A5/SCL
  N9: Mod1.pin_14, Part1.A4/SDA
  N10: Mod1.pin_15, LED1.anode
  N11: Mod1.pin_16, R1.pin_0, R2.Pin_1
  N12: Mod1.pin_30, YwRobot_Power_Supply1.VCC#5, YwRobot_Power_Supply1.VCC#6, R1.pin_1
  N13: Part1.D8, Keypad4x2.Pin6
  N14: Part1.D9_PWM, Keypad4x2.Pin5
  N15: Part1.D2, Keypad4x2.Pin4
  N16: Part1.D3_PWM, Keypad4x2.Pin3
  N17: Part1.D4, Keypad4x2.Pin2
  N18: Part1.D5_PWM, Keypad4x2.Pin1
  N19: Part1.D6_PWM, Keypad4x2.Pin8
  N20: Part1.D7, Keypad4x2.Pin7
  N21: Part1.5V, YwRobot_Power_Supply1.VCC#9, YwRobot_Power_Supply1.VCC#10
  N22: LED1.cathode, R3.Pin_1
  N23: LED2.cathode, R4.Pin_1

custom parts:
  Keypad Membran 4x4: Membrane Keypad 4x4 Matrix
  YwRobot Breadboard Power Supply: The YwRobot Breadboard Power Supply (MB-V2) has two power rails; they can be 5V or 3V3. Power to the module can be provided through the female USB socket or through the A10 (female) 2.1mm power jack.
  RFID-RC522-v2: A simple China made RFID-RC522 Reader; do check the pin labels, as this is a MFRC522 based clone.
